# Fritzing sketch Quadcopter Design Ver3 (saved by Fritzing 0.9.3b)
stripboards: 1

parts:
  Arduino_Nano = Arduino Nano (Rev3.0)
  GPIO1 = LED - 3mm [color="Green (555nm)" package="3 mm [THT]"]
  R1 = Resistor [tolerance=±5% resistance=68 package=THT]
  GPIO2 = LED - 3mm [color="Green (555nm)" package="3 mm [THT]"]
  R2 = Resistor [tolerance=±5% resistance=68 package=THT]
  GPIO3 = LED - 3mm [color="Green (555nm)" package="3 mm [THT]"]
  R3 = Resistor [tolerance=±5% resistance=68 package=THT]
  GPIO0 = LED - 3mm [color="Green (555nm)" package="3 mm [THT]"]
  R4 = Resistor [tolerance=±5% resistance=68 package=THT]
  LED_PIN = LED - 3mm [color="Yellow (592nm)" package="3 mm [THT]"]
  R5 = Resistor [tolerance=±5% resistance=68 package=THT]
  GND = male pin header, 3 pins [form="♂ (male)"]
  ALIE = male pin header, 1 pin [form="♂ (male)"]
  ELEV = male pin header, 1 pin [form="♂ (male)"]
  RUDD = male pin header, 1 pin [form="♂ (male)"]
  GEAR = male pin header, 1 pin [form="♂ (male)"]
  AUX1 = male pin header, 1 pin [form="♂ (male)"]
  5V = male pin header, 3 pins [form="♂ (male)"]
  M1 = male pin header, 3 pins [form="♂ (male)"]
  M2 = male pin header, 3 pins [form="♂ (male)"]
  M3 = male pin header, 3 pins [form="♂ (male)"]
  M4 = male pin header, 3 pins [form="♂ (male)"]
  MPU_6050 = female pin header, 8 pins [form="♀ (female)"]
  THRO = male pin header, 3 pins [form="♂ (male)"]
  Power_5v_BEC = male pin header, 2 pins [form="♂ (male)"]
  LED_PIN_DEBUG = male pin header, 1 pin [form="♂ (male)"]
  GPIO_DEBUG = male pin header, 1 pin [form="♂ (male)"]
  GPIO1_DEBUG = male pin header, 1 pin [form="♂ (male)"]
  GPIO2_DEBUG = male pin header, 1 pin [form="♂ (male)"]
  GPIO0_DEBUG = male pin header, 1 pin [form="♂ (male)"]
  Jumper = male pin header, 2 pins [form="♂ (male)"]

nets (from the schematic view):
  GND/MPU6050_GND: Arduino_Nano.GND, GPIO1.cathode, GPIO2.cathode, GPIO3.cathode, GPIO0.cathode, LED_PIN.cathode, GND.pin1, GND.pin2, GND.pin3, M1.pin3, M2.pin3, M3.pin3, M4.pin3, MPU_6050.pin2, THRO.pin1, Power_5v_BEC.pin2
  THRO: Arduino_Nano.D2, THRO.pin3
  M1: Arduino_Nano.D3, M1.pin1
  ALIE: Arduino_Nano.D4, ALIE.pin1
  M2: Arduino_Nano.D5, M2.pin1
  M3: Arduino_Nano.D6, M3.pin1
  ELEV: Arduino_Nano.D7, ELEV.pin1
  RUDD: Arduino_Nano.D8, RUDD.pin1
  GEAR: Arduino_Nano.D9, GEAR.pin1
  AUX1: Arduino_Nano.D10, AUX1.pin1
  M4: Arduino_Nano.D11/MOSI, M4.pin1
  MPU6050_INT: Arduino_Nano.D12/MISO, MPU_6050.pin8
  5v In: Arduino_Nano.VIN, 5V.pin1, 5V.pin2, 5V.pin3, Power_5v_BEC.pin1
  5v Out/MPU6050_VCC: Arduino_Nano.5V, MPU_6050.pin1, THRO.pin2
  MPU6050_SCL: Arduino_Nano.A5, MPU_6050.pin3
  MPU6050_SDA: Arduino_Nano.A4, MPU_6050.pin4
  GPIO3: Arduino_Nano.A3, GPIO2_DEBUG.pin1, Jumper.pin1
  GPIO2: Arduino_Nano.A2, R2.Pin_0, GPIO1_DEBUG.pin1
  GPIO1: Arduino_Nano.A1, R1.Pin_0, GPIO0_DEBUG.pin1
  GPIO0: Arduino_Nano.A0, R4.Pin_0, GPIO_DEBUG.pin1
  LED_PIN: Arduino_Nano.D13/SCK, R5.Pin_0, LED_PIN_DEBUG.pin1
  N1: GPIO1.anode, R1.Pin_1
  N2: GPIO2.anode, R2.Pin_1
  N3: GPIO3.anode, R3.Pin_1
  N4: R3.Pin_0, Jumper.pin2
  N5: GPIO0.anode, R4.Pin_1
  N6: LED_PIN.anode, R5.Pin_1

notes:
  Jumper ON = DO.
  Jumper OFF = AI
