# Fritzing sketch Quadcopter Schematic Rev 001 (saved by Fritzing 0.9.2b)
circuit board: 7.5cm x 7.5cm
stripboards: 1

parts:
  Arduino_Nano = Arduino Nano (Rev3.0)
  IMU = screw terminal, 4 pins
  THRO = male pin header, 3 pins [form="♂ (male)"]
  RUDD = male pin header, 3 pins [form="♂ (male)"]
  ELEV = male pin header, 3 pins [form="♂ (male)"]
  ALIE = male pin header, 3 pins [form="♂ (male)"]
  AUX = male pin header, 3 pins [form="♂ (male)"]
  M1 = male pin header, 3 pins [form="♂ (male)"]
  M2 = male pin header, 3 pins [form="♂ (male)"]
  M3 = male pin header, 3 pins [form="♂ (male)"]
  M4 = male pin header, 3 pins [form="♂ (male)"]
  Digital_IO = screw terminal, 3 pins
  5v_out = screw terminal, 4 pins  # not connected

nets (from the pcb view):
  N1: Arduino_Nano.GND, IMU.pin4, THRO.pin3, RUDD.pin3, ELEV.pin3, ALIE.pin3, AUX.pin3, M1.pin3, M2.pin3, M3.pin3, M4.pin3
  N2: Arduino_Nano.D2, THRO.pin1
  N3: Arduino_Nano.D3, M1.pin1
  N4: Arduino_Nano.D4, RUDD.pin1
  N5: Arduino_Nano.D5, M2.pin1
  N6: Arduino_Nano.D6, M3.pin1
  N7: Arduino_Nano.D7, ELEV.pin1
  N8: Arduino_Nano.D8, ALIE.pin1
  N9: Arduino_Nano.D9, AUX.pin1
  N10: Arduino_Nano.D10, Digital_IO.pin1
  N11: Arduino_Nano.D11/MOSI, M4.pin1
  N12: Arduino_Nano.D12/MISO, Digital_IO.pin2
  N13: Arduino_Nano.VIN, THRO.pin2, M4.pin2
  N14: Arduino_Nano.A5, IMU.pin1
  N15: Arduino_Nano.A4, IMU.pin2
  N16: Arduino_Nano.3V3, IMU.pin3
  N17: Arduino_Nano.D13/SCK, Digital_IO.pin3

notes:
  Quadcopter, 001
  THRO
  RUDD
  ALIE
  ELEV
  AUX
  Arduino Nano
  M1
  M2
  M3
  M4
  IMU
  SCL
  SDA
  3.3V
  GND
  DIO 0
  DIO 1
  DIO 2
  5V Out
  Quadcopter Rev 001
  width = 19holes
  Length = 24 holes
  + 2 to each dimention to allow for cutting buffer
